# Fritzing sketch schema_arduino_nuovo_alimentazione (saved by Fritzing 0.9.4)

parts:
  Part1 = Arduino Uno (Rev3)
  R1 = Resistor [tolerance=±5% resistance=220 package=THT]
  FC-1 = Sound Sensor
  U1 = AD9833 Module
  Raspberry_Pi_1 = Raspberry Pi 3 [part_number=RPI-3-V1.2]
  HLK-PM1 = HLK-PM01
  HLK-PM2 = HLK-PM12 [part_number=HLK-PM12]
  U2 = RELAY [package=relay-jzc]
  C1 = Electrolytic Capacitor [capacitance=47µF voltage=50V package="100 mil [THT, electrolytic]"]
  J1 = Screw terminal - 2 pins [package=THT]
  J2 = Screw terminal - 2 pins [package=THT]

nets:
  N1: Part1.A0, FC-1.OUT
  N2: Part1.D10_PWM/SS, U1.FSYNC
  N3: Part1.D11_PWM/MOSI, U1.SDATA
  N4: Part1.D13/SCK, U1.SCLK
  N5: Part1.D3_PWM, U2.NC
  N6: Part1.D5_PWM, R1.Pin_1
  VCC: Part1.5V, FC-1.VCC, U1.VCC
  GND: Part1.GND, FC-1.GND, U1.DGND, Raspberry_Pi_1.GND, HLK-PM1.-Vo, HLK-PM2.-Vo, U2.COIL1, J1.pin1
  N7: Part1.VIN, HLK-PM2.+Vo, U2.MAIN, J1.pin2
  N8: U1.AGND, C1.+
  N9: U1.OUT, J2.pin1
  N10: Raspberry_Pi_1.5V, HLK-PM1.+Vo

custom parts:
  AD9833 Module: programmable waveform generator
